// Logisim project cpu.circ as structural Verilog: 7 circuits, main circuit ComputeProcessingUnit
module MemoryCell (
  input  Clock,
  input  WriteEnable,
  input  DataInput,
  input  OutputEnable,
  input  Reset,
  output DataOutput,
  output StoredData
);

  wire and_1_out, and_2_out, not_1_out, or_1_out;

  not not_1 (not_1_out, WriteEnable);
  and and_1 (and_1_out, StoredData, not_1_out);
  and and_2 (and_2_out, WriteEnable, DataInput);
  or or_1 (or_1_out, and_1_out, and_2_out);
  D_Flip_Flop #(.trigger("falling")) d_ff_1 (
    .D(or_1_out), .clk(Clock), .Q(StoredData), .reset(Reset));  // open: Qn, preset
  assign DataOutput = OutputEnable ? StoredData : 1'bz;  // Controlled_Buffer controlled_buffer_1
endmodule

module Register8bits (
  input  Reset,
  input  OutputEnable,
  input  Clock,
  input  WriteEnable,
  input  [7:0] DataInput,
  output [7:0] DataOutput,
  output [7:0] StoredData
);

  MemoryCell memorycell_1 (
    .Clock(Clock), .WriteEnable(WriteEnable), .DataInput(DataInput[0]), .OutputEnable(OutputEnable),
    .Reset(Reset), .DataOutput(DataOutput[0]), .StoredData(StoredData[0]));
  MemoryCell memorycell_2 (
    .Clock(Clock), .WriteEnable(WriteEnable), .DataInput(DataInput[1]), .OutputEnable(OutputEnable),
    .Reset(Reset), .DataOutput(DataOutput[1]), .StoredData(StoredData[1]));
  MemoryCell memorycell_3 (
    .Clock(Clock), .WriteEnable(WriteEnable), .DataInput(DataInput[2]), .OutputEnable(OutputEnable),
    .Reset(Reset), .DataOutput(DataOutput[2]), .StoredData(StoredData[2]));
  MemoryCell memorycell_4 (
    .Clock(Clock), .WriteEnable(WriteEnable), .DataInput(DataInput[3]), .OutputEnable(OutputEnable),
    .Reset(Reset), .DataOutput(DataOutput[3]), .StoredData(StoredData[3]));
  MemoryCell memorycell_5 (
    .Clock(Clock), .WriteEnable(WriteEnable), .DataInput(DataInput[4]), .OutputEnable(OutputEnable),
    .Reset(Reset), .DataOutput(DataOutput[4]), .StoredData(StoredData[4]));
  MemoryCell memorycell_6 (
    .Clock(Clock), .WriteEnable(WriteEnable), .DataInput(DataInput[5]), .OutputEnable(OutputEnable),
    .Reset(Reset), .DataOutput(DataOutput[5]), .StoredData(StoredData[5]));
  MemoryCell memorycell_7 (
    .Clock(Clock), .WriteEnable(WriteEnable), .DataInput(DataInput[6]), .OutputEnable(OutputEnable),
    .Reset(Reset), .DataOutput(DataOutput[6]), .StoredData(StoredData[6]));
  MemoryCell memorycell_8 (
    .Clock(Clock), .WriteEnable(WriteEnable), .DataInput(DataInput[7]), .OutputEnable(OutputEnable),
    .Reset(Reset), .DataOutput(DataOutput[7]), .StoredData(StoredData[7]));

  // Notes on the sheet:
  //   0
  //   1
  //   2
  //   3
  //   4
  //   5
  //   6
  //   7
endmodule

module Equals (
  input  [7:0] DataInput1,
  input  [7:0] DataInput2,
  output IsEqual
);

  wire [7:0] xnor_1_out;

  assign xnor_1_out = ~(DataInput1 ^ DataInput2);  // XNOR_Gate xnor_1, 8 bits wide
  and and_1 (IsEqual, xnor_1_out[0], xnor_1_out[1], xnor_1_out[2], xnor_1_out[3], xnor_1_out[4], xnor_1_out[5], xnor_1_out[6], xnor_1_out[7]);
endmodule

module ComputeProcessingUnit (
);

  wire clock_1_out, equals_1_isequal, not_1_out;
  wire [7:0] adder_1_out, instructionexecutor_1_outputinstructionpointer,
       instructionexecutor_1_outputregistera, instructionexecutor_1_outputregisterb,
       instructionexecutor_1_outputregisterc, multiplexer_1_out, register8bits_1_storeddata,
       register8bits_2_storeddata, register8bits_3_storeddata, register8bits_4_dataoutput, rom_1_p2,
       rom_1_p3, rom_1_p4, rom_1_p5;

  Clock clock_1 (.out(clock_1_out));
  Multiplexer #(.width(8)) multiplexer_1 (
    .in0(adder_1_out), .in1(instructionexecutor_1_outputinstructionpointer), .out(multiplexer_1_out),
    .sel(not_1_out));
  not not_1 (not_1_out, equals_1_isequal);
  Equals equals_1 (
    .DataInput1(instructionexecutor_1_outputinstructionpointer), .DataInput2(register8bits_4_dataoutput),
    .IsEqual(equals_1_isequal));
  Register8bits register8bits_1 (
    .Clock(clock_1_out), .WriteEnable(clock_1_out), .DataInput(instructionexecutor_1_outputregistera),
    .StoredData(register8bits_1_storeddata));  // open: Reset, OutputEnable, DataOutput
  Register8bits register8bits_2 (
    .Clock(clock_1_out), .WriteEnable(clock_1_out), .DataInput(instructionexecutor_1_outputregisterb),
    .StoredData(register8bits_2_storeddata));  // open: Reset, OutputEnable, DataOutput
  Register8bits register8bits_3 (
    .Clock(clock_1_out), .WriteEnable(clock_1_out), .DataInput(instructionexecutor_1_outputregisterc),
    .StoredData(register8bits_3_storeddata));  // open: Reset, OutputEnable, DataOutput
  // Probe on register8bits_4_dataoutput
  Register8bits register8bits_4 (
    .OutputEnable(clock_1_out), .Clock(clock_1_out), .WriteEnable(clock_1_out),
    .DataInput(multiplexer_1_out), .DataOutput(register8bits_4_dataoutput));  // open: Reset, StoredData
  // Probe on register8bits_1_storeddata
  // Probe on register8bits_2_storeddata
  // Probe on register8bits_3_storeddata
  Adder adder_1 (.a(register8bits_4_dataoutput), .b(8'h4), .out(adder_1_out));  // open: cin, cout
  // ROM #(.line("quad")) rom_1: pin names not known; wires that end beside it: register8bits_4_dataoutput, rom_1_p2, rom_1_p3, rom_1_p4, rom_1_p5
  InstructionExecutor instructionexecutor_1 (
    .Operation(rom_1_p2), .Operand1(rom_1_p3), .Operand2(rom_1_p4), .Operand3(rom_1_p5),
    .InputRegisterA(register8bits_1_storeddata), .InputRegisterB(register8bits_2_storeddata),
    .InputRegisterC(register8bits_3_storeddata), .InputInstructionPointer(register8bits_4_dataoutput),
    .OutputRegisterA(instructionexecutor_1_outputregistera),
    .OutputRegisterB(instructionexecutor_1_outputregisterb),
    .OutputRegisterC(instructionexecutor_1_outputregisterc),
    .OutputInstructionPointer(instructionexecutor_1_outputinstructionpointer));
  // Probe on rom_1_p2
  // Probe on rom_1_p3
  // Probe on rom_1_p4
  // Probe on rom_1_p5
  // Probe on instructionexecutor_1_outputregistera
  // Probe on instructionexecutor_1_outputregisterb
  // Probe on instructionexecutor_1_outputregisterc
  // Probe on instructionexecutor_1_outputinstructionpointer

  // Notes on the sheet:
  //   contents of rom_1 (hex, n*v repeats v):
  //   6 0 8 0 6 1 2 0 1 0 1 2 8 2 0 0 7 8
endmodule

module InstructionExecutor (
  input  [7:0] Operation,
  input  [7:0] Operand1,
  input  [7:0] Operand2,
  input  [7:0] Operand3,
  input  [7:0] InputRegisterA,
  input  [7:0] InputRegisterB,
  input  [7:0] InputRegisterC,
  input  [7:0] InputInstructionPointer,
  output [7:0] OutputRegisterA,
  output [7:0] OutputRegisterB,
  output [7:0] OutputRegisterC,
  output [7:0] OutputInstructionPointer
);

  wire controlled_buffer_16_out, equals_1_isequal, equals_2_isequal, equals_3_isequal, equals_4_isequal,
       equals_5_isequal, equals_6_isequal, equals_7_isequal, equals_8_isequal, equals_9_isequal,
       ie_setregister_1_outputdisablea, ie_setregister_1_outputdisableb, ie_setregister_1_outputdisablec,
       not_1_out, or_1_out;
  wire [7:0] adder_1_out, controlled_buffer_5_out, controlled_buffer_10_out, controlled_buffer_11_out,
       divider_1_out, divider_1_rem, ie_getregister_1_outputdata, ie_getregister_2_outputdata,
       ie_getregister_3_outputdata, multiplier_1_out, subtractor_1_out;

  IE_GetRegister ie_getregister_1 (
    .SelectRegister(Operand1), .InputRegisterA(InputRegisterA), .InputRegisterB(InputRegisterB),
    .InputRegisterC(InputRegisterC), .OutputData(ie_getregister_1_outputdata));
  IE_GetRegister ie_getregister_2 (
    .SelectRegister(Operand2), .InputRegisterA(InputRegisterA), .InputRegisterB(InputRegisterB),
    .InputRegisterC(InputRegisterC), .OutputData(ie_getregister_2_outputdata));
  Equals equals_1 (.DataInput1(Operation), .DataInput2(8'h7), .IsEqual(equals_1_isequal));
  Equals equals_2 (.DataInput1(Operation), .DataInput2(8'h8), .IsEqual(equals_2_isequal));
  Equals equals_3 (.DataInput1(Operation), .DataInput2({8{1'b0}}), .IsEqual(equals_3_isequal));
  Equals equals_4 (.DataInput1(Operation), .DataInput2(8'h1), .IsEqual(equals_4_isequal));
  Equals equals_5 (.DataInput1(Operation), .DataInput2(8'h2), .IsEqual(equals_5_isequal));
  Equals equals_6 (.DataInput1(Operation), .DataInput2(8'h3), .IsEqual(equals_6_isequal));
  Equals equals_7 (.DataInput1(Operation), .DataInput2(8'h4), .IsEqual(equals_7_isequal));
  Equals equals_8 (.DataInput1(Operation), .DataInput2(8'h5), .IsEqual(equals_8_isequal));
  Equals equals_9 (.DataInput1(Operation), .DataInput2(8'h6), .IsEqual(equals_9_isequal));
  assign OutputRegisterA = ie_setregister_1_outputdisablea ? InputRegisterA : 8'bz;  // Controlled_Buffer controlled_buffer_1
  assign OutputRegisterB = ie_setregister_1_outputdisableb ? InputRegisterB : 8'bz;  // Controlled_Buffer controlled_buffer_2
  assign OutputRegisterC = ie_setregister_1_outputdisablec ? InputRegisterC : 8'bz;  // Controlled_Buffer controlled_buffer_3
  assign OutputInstructionPointer = controlled_buffer_16_out ? InputInstructionPointer : 8'bz;  // Controlled_Buffer controlled_buffer_4
  Adder adder_1 (
    .a(ie_getregister_1_outputdata), .b(ie_getregister_2_outputdata), .out(adder_1_out));  // open: cin, cout
  Subtractor subtractor_1 (
    .a(ie_getregister_1_outputdata), .b(ie_getregister_2_outputdata), .out(subtractor_1_out));  // open: bin, bout
  Multiplier multiplier_1 (
    .a(ie_getregister_1_outputdata), .b(ie_getregister_2_outputdata), .out(multiplier_1_out));  // open: cin, cout
  Divider divider_1 (
    .a(ie_getregister_1_outputdata), .b(ie_getregister_2_outputdata), .out(divider_1_out), .rem(divider_1_rem));  // open: upper
  assign controlled_buffer_5_out = equals_4_isequal ? adder_1_out : 8'bz;  // Controlled_Buffer controlled_buffer_5
  assign controlled_buffer_5_out = equals_5_isequal ? subtractor_1_out : 8'bz;  // Controlled_Buffer controlled_buffer_6
  assign controlled_buffer_5_out = equals_6_isequal ? multiplier_1_out : 8'bz;  // Controlled_Buffer controlled_buffer_7
  assign controlled_buffer_5_out = equals_7_isequal ? divider_1_out : 8'bz;  // Controlled_Buffer controlled_buffer_8
  assign controlled_buffer_5_out = equals_8_isequal ? divider_1_rem : 8'bz;  // Controlled_Buffer controlled_buffer_9
  assign controlled_buffer_10_out = equals_9_isequal ? Operand2 : 8'bz;  // Controlled_Buffer controlled_buffer_10
  IE_GetRegister ie_getregister_3 (
    .SelectRegister(Operand1), .InputRegisterA(InputRegisterA), .InputRegisterB(InputRegisterB),
    .InputRegisterC(InputRegisterC), .OutputData(ie_getregister_3_outputdata));
  or or_1 (or_1_out, equals_4_isequal, equals_5_isequal, equals_6_isequal, equals_7_isequal, equals_8_isequal);
  assign controlled_buffer_11_out = equals_2_isequal ? ie_getregister_3_outputdata : 8'bz;  // Controlled_Buffer controlled_buffer_11
  IE_SetRegister ie_setregister_1 (
    .Enable(equals_9_isequal), .InputData(controlled_buffer_10_out), .SelectRegister(Operand1),
    .OutputRegisterA(OutputRegisterA), .OutputRegisterB(OutputRegisterB), .OutputRegisterC(OutputRegisterC),
    .OutputDisableA(ie_setregister_1_outputdisablea), .OutputDisableB(ie_setregister_1_outputdisableb),
    .OutputDisableC(ie_setregister_1_outputdisablec));
  assign OutputInstructionPointer = equals_1_isequal ? Operand1 : 8'bz;  // Controlled_Buffer controlled_buffer_12
  IE_SetRegister ie_setregister_2 (
    .Enable(or_1_out), .InputData(controlled_buffer_5_out), .SelectRegister(Operand3),
    .OutputRegisterA(OutputRegisterA), .OutputRegisterB(OutputRegisterB), .OutputRegisterC(OutputRegisterC),
    .OutputDisableA(ie_setregister_1_outputdisablea), .OutputDisableB(ie_setregister_1_outputdisableb),
    .OutputDisableC(ie_setregister_1_outputdisablec));
  not not_1 (not_1_out, equals_1_isequal);
  assign ie_setregister_1_outputdisablea = equals_3_isequal ? equals_3_isequal : 1'bz;  // Controlled_Buffer controlled_buffer_13
  assign ie_setregister_1_outputdisableb = equals_3_isequal ? equals_3_isequal : 1'bz;  // Controlled_Buffer controlled_buffer_14
  assign ie_setregister_1_outputdisablec = equals_3_isequal ? equals_3_isequal : 1'bz;  // Controlled_Buffer controlled_buffer_15
  assign controlled_buffer_16_out = not_1_out ? 1'b1 : 1'bz;  // Controlled_Buffer controlled_buffer_16
  assign ie_setregister_1_outputdisablea = equals_1_isequal ? equals_1_isequal : 1'bz;  // Controlled_Buffer controlled_buffer_17
  assign ie_setregister_1_outputdisableb = equals_1_isequal ? equals_1_isequal : 1'bz;  // Controlled_Buffer controlled_buffer_18
  assign ie_setregister_1_outputdisablec = equals_1_isequal ? equals_1_isequal : 1'bz;  // Controlled_Buffer controlled_buffer_19
  IE_SetRegister ie_setregister_3 (
    .Enable(equals_2_isequal), .InputData(controlled_buffer_11_out), .SelectRegister(Operand2),
    .OutputRegisterA(OutputRegisterA), .OutputRegisterB(OutputRegisterB), .OutputRegisterC(OutputRegisterC),
    .OutputDisableA(ie_setregister_1_outputdisablea), .OutputDisableB(ie_setregister_1_outputdisableb),
    .OutputDisableC(ie_setregister_1_outputdisablec));

  // Notes on the sheet:
  //   JUMP
  //   MOVE
  //   NOOP
  //   ADD
  //   SUB
  //   MUL
  //   DIV
  //   REM
  //   IMMEDIATE
endmodule

module IE_SetRegister (
  input  Enable,
  input  [7:0] InputData,
  input  [7:0] SelectRegister,
  output [7:0] OutputRegisterA,
  output [7:0] OutputRegisterB,
  output [7:0] OutputRegisterC,
  output OutputDisableA,
  output OutputDisableB,
  output OutputDisableC
);

  wire controlled_inverter_1_out, controlled_inverter_2_out, controlled_inverter_3_out, demultiplexer_1_out0,
       demultiplexer_1_out1, demultiplexer_1_out2, or_1_out, or_2_out, or_3_out;
  wire [7:0] controlled_buffer_1_out, demultiplexer_2_out0, demultiplexer_2_out1, demultiplexer_2_out2;

  assign controlled_buffer_1_out = Enable ? InputData : 8'bz;  // Controlled_Buffer controlled_buffer_1
  Demultiplexer #(.select(2)) demultiplexer_1 (
    .out0(demultiplexer_1_out0), .out1(demultiplexer_1_out1), .out2(demultiplexer_1_out2), .in(Enable),
    .sel(SelectRegister[1:0]));  // open: out3
  Demultiplexer #(.select(2), .width(8)) demultiplexer_2 (
    .out0(demultiplexer_2_out0), .out1(demultiplexer_2_out1), .out2(demultiplexer_2_out2),
    .in(controlled_buffer_1_out), .sel(SelectRegister[1:0]));  // open: out3
  or or_1 (or_1_out, demultiplexer_1_out1, demultiplexer_1_out2);
  or or_2 (or_2_out, demultiplexer_1_out0, demultiplexer_1_out2);
  or or_3 (or_3_out, demultiplexer_1_out1, demultiplexer_1_out0);
  assign OutputDisableA = or_1_out ? Enable : 1'bz;  // Controlled_Buffer controlled_buffer_2
  assign OutputDisableB = or_2_out ? Enable : 1'bz;  // Controlled_Buffer controlled_buffer_3
  assign OutputDisableC = or_3_out ? Enable : 1'bz;  // Controlled_Buffer controlled_buffer_4
  assign OutputRegisterA = controlled_inverter_1_out ? demultiplexer_2_out0 : 8'bz;  // Controlled_Buffer controlled_buffer_5
  assign controlled_inverter_1_out = Enable ? ~or_1_out : 1'bz;  // Controlled_Inverter controlled_inverter_1
  assign OutputRegisterB = controlled_inverter_2_out ? demultiplexer_2_out1 : 8'bz;  // Controlled_Buffer controlled_buffer_6
  assign controlled_inverter_2_out = Enable ? ~or_2_out : 1'bz;  // Controlled_Inverter controlled_inverter_2
  assign OutputRegisterC = controlled_inverter_3_out ? demultiplexer_2_out2 : 8'bz;  // Controlled_Buffer controlled_buffer_7
  assign controlled_inverter_3_out = Enable ? ~or_3_out : 1'bz;  // Controlled_Inverter controlled_inverter_3
endmodule

module IE_GetRegister (
  input  [7:0] SelectRegister,
  input  [7:0] InputRegisterA,
  input  [7:0] InputRegisterB,
  input  [7:0] InputRegisterC,
  output [7:0] OutputData
);

  Multiplexer #(.select(2), .width(8)) multiplexer_1 (
    .in0(InputRegisterA), .in1(InputRegisterB), .in2(InputRegisterC), .out(OutputData),
    .sel(SelectRegister[1:0]));  // open: in3
endmodule
